# Fritzing sketch DiagramaDeConexion (saved by Fritzing 0.9.3b)
breadboards: 1

parts:
  Componente1 = Arduino Uno (Rev3)
  L1 = Solenoid
  S1 = Toggle Switch [package=THT]
  S2 = Toggle Switch [package=THT]
  S3 = Toggle Switch [package=THT]
  R1 = Photocell (LDR) [package=THT]
  Componente2 = Bluetooth HC-05 Macho
  LED1 = LED - 5mm [color="Green (555nm)" package="5 mm [THT]"]
  LED3 = LED - 5mm [color="White (8000K)" package="5 mm [THT]"]
  VCC1 = Battery  # not connected
  VCC2 = Battery  # not connected
  VCC3 = Battery
  Part1 = KY-019 5V Relay Module [package="Breakout board"]
  Part2 = KY-015 Temperature & Humidity Sensor Module [package="Breakout board"]
  J5 = shrouded pin header, 6 pins [form="♂ (shrouded male)"]
  J6 = shrouded pin header, 6 pins [form="♂ (shrouded male)"]
  VCC4 = 4 x AAA Battery Mount
  R2 = Resistor [tolerance=±5% resistance=220 package=THT]
  R3 = Resistor [tolerance=±5% resistance=220 package=THT]
  R4 = Resistor [tolerance=±5% resistance=220k package=THT]
  R5 = Resistor [tolerance=±5% resistance=4.7k package=THT]
  R6 = Resistor [tolerance=±5% resistance=4.7k package=THT]  # not connected
  R7 = Resistor [tolerance=±5% resistance=4.7k package=THT]
  J7 = Piezo Speaker
  LED4 = LED - 5mm [color="Red (633nm)" package="5 mm [THT]"]

nets:
  N1: Componente1.A4/SDA, R1.pin_0, R4.Pin_1
  N2: Componente1.D8, Part1.+
  N3: Componente1.D9_PWM, LED3.cathode
  N4: Componente1.D10_PWM/SS, Componente2.TXD
  N5: Componente1.D11_PWM/MOSI, Componente2.RXD
  N6: Componente1.D12/MISO, R3.Pin_0, R3.Pin_1, LED4.cathode
  N7: Componente1.GND, S1.L1, S2.L1, S3.L1, LED1.anode, LED3.anode, Part2.S, J5.pin3, R4.Pin_0, J7.pin1, LED4.anode
  N8: Componente1.D2, Part2.Vin
  N9: Componente1.D3_PWM, S1.L2, R5.Pin_1
  N10: Componente1.D4, J7.pin2
  N11: Componente1.D5_PWM, S2.L2
  N12: Componente1.D6_PWM, S3.L2, R7.Pin_1
  N13: Componente1.D7, LED1.cathode, R2.Pin_0, R2.Pin_1
  N14: Componente1.5V, R1.pin_1, Part2.-, R5.Pin_0, R7.Pin_0
  N15: L1.pin1, Part1.NC
  N16: Componente2.VCC, J6.pin2, VCC4.+
  N17: Componente2.GND, J5.pin2
  N18: VCC3.+, Part1.Common
  N19: Part1.S, J6.pin3
  N20: Part1.-, J5.pin5, VCC4.-

custom parts:
  KY-019 5V Relay Module: KY-019 5V Relay module, used to control AC circuits.
  KY-015 Temperature & Humidity Sensor Module: KY-015 temperature and humidity sensor module, provides a low-latency serial interface to measure humidity and temperature.
