# Fritzing sketch botiquin_luces_y_pulsador (saved by Fritzing 0.9.3b)
breadboards: 1

parts:
  LED1 = LED - 5mm [color="Blue (430nm)" package="5 mm [THT]"]
  R1 = Resistor [tolerance=±5% resistance=220 package=THT]
  Componente1 = Arduino Uno (Rev3)
  LED2 = LED - 5mm [color="Red (633nm)" package="5 mm [THT]"]
  R2 = Resistor [tolerance=±5% resistance=220 package=THT]

nets:
  N1: LED1.cathode, Componente1.GND, LED2.cathode
  N2: LED1.anode, R1.Pin_0
  N3: R1.Pin_1, Componente1.D5_PWM
  N4: Componente1.D4, R2.Pin_1
  N5: LED2.anode, R2.Pin_0
